// Logisim project Dual Core Project.circ as structural Verilog: 5 circuits, main circuit main
module main (
  input  [7:0] my_data,
  input  enb,
  input  [7:0] Data,
  input  [1:0] enb_2,
  output [7:0] my_address,
  output [7:0] Adds
);

  wire clock_1_out, control_1_acc_to_mem, decoder_1_out3, decoder_1_out4, decoder_1_out5, decoder_1_out6,
       decoder_1_out7, nand_1_out, not_1_out, not_2_out, or_1_out;
  wire [1:0] control_1_acc_data2, control_1_alus2;
  wire [7:0] ACC_q, adder_1_out, alu_1_out_4, bit_extender_1_out, controlled_buffer_2_out, multiplexer_1_out,
       multiplexer_2_out, multiplexer_3_out, undriven;

  Adder adder_1 (.a(Adds), .b(multiplexer_3_out), .out(adder_1_out));  // open: cin, cout
  Decoder #(.select(3)) decoder_1 (
    .out3(decoder_1_out3), .out4(decoder_1_out4), .out5(decoder_1_out5), .out6(decoder_1_out6),
    .out7(decoder_1_out7), .sel(Data[7:5]));  // open: out0, out1, out2, en
  Register PC (.D(adder_1_out), .Q(Adds), .clk(clock_1_out));  // open: en, clr
  Clock clock_1 (.out(clock_1_out));
  or or_1 (or_1_out, decoder_1_out3, decoder_1_out4, decoder_1_out5, decoder_1_out6, decoder_1_out7);
  Multiplexer #(.width(8), .enable("false")) multiplexer_1 (
    .in0(my_data), .in1(controlled_buffer_2_out), .out(multiplexer_1_out), .sel(enb));
  assign my_address = not_1_out ? multiplexer_1_out : 8'bz;  // Controlled_Buffer controlled_buffer_1
  RAM #(.addrWidth(5)) ram_1 (
    .addr(Data[4:0]), .data(my_address), .clk(clock_1_out), .ld(control_1_acc_to_mem));  // open: sel, clr
  not not_1 (not_1_out, control_1_acc_to_mem);
  assign bit_extender_1_out = {{3{1'b0}}, Data[4:0]};  // Bit_Extender bit_extender_1
  control control_1 (
    .OP3(Data[7]), .OP2(Data[6]), .OP1(Data[5]), .enb(enb_2), .AluS(control_1_alus2[1]),
    .AluS2(control_1_alus2[0]), .ACC_to_Mem(control_1_acc_to_mem), .ACC_Data1(control_1_acc_data2[1]),
    .ACC_Data2(control_1_acc_data2[0]));  // open: DM_Sel, DM_LD
  Multiplexer #(.select(2), .width(8)) multiplexer_2 (
    .in0(my_address), .in1(bit_extender_1_out), .in2(alu_1_out_4), .in3(undriven), .out(multiplexer_2_out),
    .sel(control_1_acc_data2));  // open: en
  Register ACC (.D(multiplexer_2_out), .en(or_1_out), .Q(ACC_q), .clk(clock_1_out));  // open: clr
  Multiplexer #(.width(8)) multiplexer_3 (
    .in0(bit_extender_1_out), .in1(8'h1), .out(multiplexer_3_out), .sel(nand_1_out));  // open: en
  assign controlled_buffer_2_out = not_2_out ? ACC_q : 8'bz;  // Controlled_Buffer controlled_buffer_2
  not not_2 (not_2_out, control_1_acc_to_mem);
  ALU alu_1 (.a(my_address), .b(ACC_q), .out_4(alu_1_out_4), .S_ALU(control_1_alus2));
  nand nand_1 (nand_1_out, control_1_alus2[1], control_1_alus2[0]);

  // Notes on the sheet:
  //   IM
  //   DM
endmodule

module ALU (
  input  [7:0] a,
  input  [7:0] b,
  input  [1:0] S_ALU,
  output [7:0] out_4
);

  wire comparator_1_eq, comparator_1_gt, or_1_out;
  wire [7:0] adder_1_out, bit_extender_1_out, shifter_1_out, subtractor_1_out;

  Adder adder_1 (.a(a), .b(b), .out(adder_1_out));  // open: cin, cout
  Subtractor subtractor_1 (.a(b), .b(a), .out(subtractor_1_out));  // open: bin, bout
  Shifter #(.shift("rl")) shifter_1 (.in(a), .\dist (b[2:0]), .out(shifter_1_out));
  Comparator comparator_1 (.a(a), .b(b), .gt(comparator_1_gt), .eq(comparator_1_eq));  // open: lt
  or or_1 (or_1_out, comparator_1_gt, comparator_1_eq);
  Multiplexer #(.select(2), .width(8)) multiplexer_1 (
    .in0(adder_1_out), .in1(subtractor_1_out), .in2(shifter_1_out), .in3(bit_extender_1_out), .out(out_4),
    .sel(S_ALU));  // open: en
  assign bit_extender_1_out = {{7{1'b0}}, or_1_out};  // Bit_Extender bit_extender_1
endmodule

module Dual_Core (
);

  wire cmu_1_enable;
  wire [1:0] cmu_1_out_5, cmu_1_out_6;
  wire [7:0] cmu_1_c1o2, cmu_1_c2o2, cmu_1_core1input1, cmu_1_core2input1, main_1_adds, main_1_my_address,
       main_2_adds, main_2_my_address;
  wire [10:0] rom_1_data, rom_2_data;

  main main_1 (
    .Data(cmu_1_core1input1), .Adds(main_1_adds), .my_data(main_2_my_address), .enb(cmu_1_enable),
    .my_address(main_1_my_address), .enb_2(cmu_1_out_6));
  main main_2 (
    .Data(cmu_1_core2input1), .Adds(main_2_adds), .my_data(main_1_my_address), .enb(cmu_1_enable),
    .my_address(main_2_my_address), .enb_2(cmu_1_out_5));
  CMU cmu_1 (
    .C1O1(rom_1_data), .Enable(cmu_1_enable), .C1O2(cmu_1_c1o2), .Core1Input2(main_1_adds),
    .C2O1(rom_2_data), .C2O2(cmu_1_c2o2), .Core2Input2(main_2_adds), .out_5(cmu_1_out_5),
    .out_6(cmu_1_out_6), .Core1Input1(cmu_1_core1input1), .Core2Input1(cmu_1_core2input1));  // open: Core1_Check, C1_Select, Core2_Check, C2_Select
  ROM #(.dataWidth(11)) rom_1 (.addr(cmu_1_c1o2), .data(rom_1_data));  // open: sel
  ROM #(.dataWidth(11)) rom_2 (.addr(cmu_1_c2o2), .data(rom_2_data));  // open: sel
endmodule

// ROM 0
module CMU (
  input  [10:0] C1O1,
  input  [7:0] Core1Input2,
  input  [10:0] C2O1,
  input  [7:0] Core2Input2,
  output [1:0] out_5,
  output [1:0] out_6,
  output [4:0] C1_Select,
  output Core1_Check,
  output [7:0] Core1Input1,
  output Enable,
  output [7:0] C1O2,
  output [7:0] Core2Input1,
  output [7:0] C2O2,
  output [4:0] C2_Select,
  output Core2_Check
);

  wire not_2_out, not_3_out, xor_1_out;
  wire [7:0] bit_extender_1_out, bit_extender_2_out;

  Multiplexer #(.width(8), .enable("false")) multiplexer_1 (
    .in0(bit_extender_1_out), .in1(C1O1[7:0]), .out(Core1Input1), .sel(Enable));
  not not_1 (Enable, xor_1_out);
  Multiplexer #(.width(8), .enable("false")) multiplexer_2 (
    .in0(bit_extender_2_out), .in1(C2O1[7:0]), .out(Core2Input1), .sel(Enable));
  assign bit_extender_1_out = {{3{1'b0}}, C1_Select};  // Bit_Extender bit_extender_1
  assign bit_extender_2_out = {{3{1'b0}}, C2_Select};  // Bit_Extender bit_extender_2
  xor xor_1 (xor_1_out, C1O1[10], C2O1[10]);
  Multiplexer #(.width(5)) multiplexer_3 (
    .in0(C2O1[9:5]), .in1(C1O1[4:0]), .out(C2_Select), .sel(not_2_out));  // open: en
  not not_2 (not_2_out, C2O1[10]);
  Multiplexer #(.width(5)) multiplexer_4 (
    .in0(C1O1[9:5]), .in1(C2O1[4:0]), .out(C1_Select), .sel(not_3_out));  // open: en
  not not_3 (not_3_out, C1O1[10]);
  Multiplexer #(.select(2), .width(2), .enable("false")) multiplexer_5 (
    .in0(2'b11), .in1(2'b10), .in2(2'b01), .out(out_5), .sel({C1O1[10], C2O1[10]}));  // open: in3
  Multiplexer #(.select(2), .width(2), .enable("false")) multiplexer_6 (
    .in0(2'b11), .in1(2'b01), .in2(2'b10), .in3(2'b01), .out(out_6), .sel({C1O1[10], C2O1[10]}));

  assign C1O2 = Core1Input2;
  assign C2O2 = Core2Input2;
  assign Core1_Check = C1O1[10];
  assign Core2_Check = C2O1[10];
endmodule

module control (
  input  OP3,
  input  OP2,
  input  OP1,
  input  [1:0] enb,
  output AluS,
  output AluS2,
  output ACC_to_Mem,
  output ACC_Data1,
  output ACC_Data2,
  output DM_Sel,
  output DM_LD
);

  wire and_1_out, and_2_out, and_3_out, and_4_out, and_5_out, and_6_out, and_7_out, and_8_out, and_9_out,
       and_10_out, and_11_out, and_12_out, and_19_out, not_1_out, not_2_out, not_3_out, not_4_out, not_5_out,
       not_6_out, not_7_out, not_8_out, not_9_out, not_10_out, or_1_out, or_2_out, or_3_out, or_4_out,
       or_5_out, or_6_out, or_7_out;

  not not_1 (not_1_out, OP3);
  not not_2 (not_2_out, OP2);
  not not_3 (not_3_out, OP3);
  not not_4 (not_4_out, OP3);
  not not_5 (not_5_out, OP2);
  not not_6 (not_6_out, OP2);
  and and_1 (and_1_out, OP2, OP1);
  and and_2 (and_2_out, OP3, OP2);
  not not_7 (not_7_out, OP2);
  not not_8 (not_8_out, OP1);
  not not_9 (not_9_out, OP1);
  and and_3 (and_3_out, OP3, OP1);
  and and_4 (and_4_out, OP3, OP2);
  and and_5 (and_5_out, not_1_out, not_2_out);
  and and_6 (and_6_out, not_3_out, OP1);
  and and_7 (and_7_out, not_4_out, not_5_out);
  and and_8 (and_8_out, OP3, OP2, OP1);
  or or_1 (or_1_out, not_6_out, OP1, OP3);
  or or_2 (or_2_out, and_1_out, and_2_out);
  and and_9 (and_9_out, OP3, not_7_out, not_8_out);
  and and_10 (and_10_out, OP2, not_9_out);
  and and_11 (and_11_out, OP3, OP2);
  or or_3 (or_3_out, and_3_out, and_4_out);
  or or_4 (or_4_out, and_5_out, and_6_out);
  or or_5 (or_5_out, and_7_out, and_8_out);
  or or_6 (or_6_out, and_10_out, and_11_out);
  and and_12 (and_12_out, enb[0], enb[1]);
  not not_10 (not_10_out, enb[0]);
  and and_13 (AluS, or_4_out, and_12_out);
  and and_14 (AluS2, or_5_out, and_12_out);
  and and_15 (ACC_Data1, or_2_out, and_12_out);
  and and_16 (ACC_Data2, and_9_out, and_12_out);
  and and_17 (DM_Sel, or_6_out, and_12_out);
  and and_18 (DM_LD, or_3_out, and_12_out);
  and and_19 (and_19_out, not_10_out, enb[1]);
  or or_7 (or_7_out, and_12_out, and_19_out);
  and and_20 (ACC_to_Mem, or_1_out, or_7_out);
endmodule
